// Logisim project Projeto.circ as structural Verilog: 9 circuits, main circuit main
module somador_1bit (
  input  cin,
  input  A,
  input  B,
  output S,
  output cout
);

  wire and_1_out, and_2_out, xor_1_out;

  xor xor_1 (xor_1_out, A, B);
  and and_1 (and_1_out, A, B);
  xor xor_2 (S, cin, xor_1_out);
  and and_2 (and_2_out, cin, xor_1_out);
  or or_1 (cout, and_2_out, and_1_out);
endmodule

module main (
  input  [1:0] xy,
  input  [3:0] B,
  input  [3:0] A,
  input  [2:0] in_4,
  output out_5,
  output out_6,
  output [3:0] out_7
);

  wire dec_3x8_1_s0, dec_3x8_1_s1, dec_3x8_1_s2, dec_3x8_1_s3;
  wire [3:0] rot_dir_1_abcd_2, rot_esq_1_abcd_2, somador_4bit_1_s, subtrator_4bit_1_s;

  Dec_3x8 dec_3x8_1 (
    .ABC(in_4), .S0(dec_3x8_1_s0), .S1(dec_3x8_1_s1), .S2(dec_3x8_1_s2), .S3(dec_3x8_1_s3));  // open: S4, S5, S6, S7
  somador_4bit somador_4bit_1 (.A(A), .Overflow(out_5), .B(B), .S(somador_4bit_1_s));
  Buff buff_1 (.E(somador_4bit_1_s), .in_2(dec_3x8_1_s0), .S(out_7));
  subtrator_4bit subtrator_4bit_1 (.A(A), .Overflow(out_6), .B(B), .S(subtrator_4bit_1_s));
  Buff buff_2 (.E(subtrator_4bit_1_s), .in_2(dec_3x8_1_s1), .S(out_7));
  Rot_Esq rot_esq_1 (.abcd(A), .xy(xy), .ABCD_2(rot_esq_1_abcd_2));
  Rot_Dir rot_dir_1 (.abcd(A), .xy(xy), .ABCD_2(rot_dir_1_abcd_2));
  Buff buff_3 (.E(rot_dir_1_abcd_2), .in_2(dec_3x8_1_s2), .S(out_7));
  Buff buff_4 (.E(rot_esq_1_abcd_2), .in_2(dec_3x8_1_s3), .S(out_7));
endmodule

module somador_4bit (
  input  [3:0] B,
  input  [3:0] A,
  output Overflow,
  output [3:0] S
);

  wire somador_1bit_2_cout, somador_1bit_3_cout, somador_1bit_4_cout;

  somador_1bit somador_1bit_1 (.cin(somador_1bit_2_cout), .A(A[3]), .B(B[3]), .S(S[3]), .cout(Overflow));
  somador_1bit somador_1bit_2 (.cin(somador_1bit_3_cout), .A(A[2]), .B(B[2]), .S(S[2]), .cout(somador_1bit_2_cout));
  somador_1bit somador_1bit_3 (.cin(somador_1bit_4_cout), .A(A[1]), .B(B[1]), .S(S[1]), .cout(somador_1bit_3_cout));
  somador_1bit somador_1bit_4 (.cin(1'b0), .A(A[0]), .B(B[0]), .S(S[0]), .cout(somador_1bit_4_cout));
endmodule

module subtrator_1bit (
  input  A,
  input  B,
  input  C,
  output S,
  output Vai_1
);

  wire and_1_out, and_2_out, or_1_out, xor_1_out;

  xor xor_1 (xor_1_out, C, B);
  or or_1 (or_1_out, C, B);
  xor xor_2 (S, xor_1_out, A);
  and and_1 (and_1_out, or_1_out, ~A);  // AND_Gate
  and and_2 (and_2_out, C, B);
  or or_2 (Vai_1, and_1_out, and_2_out);
endmodule

module subtrator_4bit (
  input  [3:0] B,
  input  [3:0] A,
  output Overflow,
  output [3:0] S
);

  wire subtrator_1bit_2_vai_1, subtrator_1bit_3_vai_1, subtrator_1bit_4_vai_1;

  subtrator_1bit subtrator_1bit_1 (.S(S[3]), .Vai_1(Overflow), .A(A[3]), .B(B[3]), .C(subtrator_1bit_2_vai_1));
  subtrator_1bit subtrator_1bit_2 (
    .S(S[2]), .Vai_1(subtrator_1bit_2_vai_1), .A(A[2]), .B(B[2]), .C(subtrator_1bit_3_vai_1));
  subtrator_1bit subtrator_1bit_3 (
    .S(S[1]), .Vai_1(subtrator_1bit_3_vai_1), .A(A[1]), .B(B[1]), .C(subtrator_1bit_4_vai_1));
  subtrator_1bit subtrator_1bit_4 (.S(S[0]), .Vai_1(subtrator_1bit_4_vai_1), .A(A[0]), .B(B[0]), .C(1'b0));
endmodule

module Rot_Esq (
  input  [3:0] abcd,
  input  [1:0] xy,
  output [3:0] ABCD_2
);

  wire and_1_out, and_2_out, and_3_out, and_4_out, and_5_out, and_6_out, and_7_out, and_8_out, and_9_out;

  and and_1 (and_1_out, ~xy[1], ~xy[0], abcd[3]);  // AND_Gate
  and and_2 (and_2_out, ~xy[1], xy[0], abcd[2]);  // AND_Gate
  and and_3 (and_3_out, xy[1], ~xy[0], abcd[1]);  // AND_Gate
  and and_4 (and_4_out, xy[1], xy[0], abcd[0]);
  and and_5 (and_5_out, ~xy[1], ~xy[0], abcd[2]);  // AND_Gate
  and and_6 (and_6_out, ~xy[1], xy[0], abcd[1]);  // AND_Gate
  and and_7 (and_7_out, xy[1], ~xy[0], abcd[0]);  // AND_Gate
  and and_8 (and_8_out, ~xy[1], ~xy[0], abcd[1]);  // AND_Gate
  and and_9 (and_9_out, ~xy[1], xy[0], abcd[0]);  // AND_Gate
  and and_10 (ABCD_2[0], ~xy[1], ~xy[0], abcd[0]);  // AND_Gate
  or or_1 (ABCD_2[3], and_1_out, and_2_out, and_3_out, and_4_out);
  or or_2 (ABCD_2[2], and_5_out, and_6_out, and_7_out);
  or or_3 (ABCD_2[1], and_8_out, and_9_out);
endmodule

module Rot_Dir (
  input  [3:0] abcd,
  input  [1:0] xy,
  output [3:0] ABCD_2
);

  wire and_1_out, and_2_out, and_3_out, and_4_out, and_5_out, and_6_out, and_7_out, and_8_out, and_9_out;

  and and_1 (and_1_out, ~xy[1], ~xy[0], abcd[0]);  // AND_Gate
  and and_2 (and_2_out, ~xy[1], xy[0], abcd[1]);  // AND_Gate
  and and_3 (and_3_out, xy[1], ~xy[0], abcd[2]);  // AND_Gate
  and and_4 (and_4_out, xy[1], xy[0], abcd[3]);
  and and_5 (and_5_out, ~xy[1], ~xy[0], abcd[1]);  // AND_Gate
  and and_6 (and_6_out, ~xy[1], xy[0], abcd[2]);  // AND_Gate
  and and_7 (and_7_out, xy[1], ~xy[0], abcd[3]);  // AND_Gate
  and and_8 (and_8_out, ~xy[1], ~xy[0], abcd[2]);  // AND_Gate
  and and_9 (and_9_out, ~xy[1], xy[0], abcd[3]);  // AND_Gate
  and and_10 (ABCD_2[3], ~xy[1], ~xy[0], abcd[3]);  // AND_Gate
  or or_1 (ABCD_2[0], and_1_out, and_2_out, and_3_out, and_4_out);
  or or_2 (ABCD_2[1], and_5_out, and_6_out, and_7_out);
  or or_3 (ABCD_2[2], and_8_out, and_9_out);
endmodule

module Dec_3x8 (
  input  [2:0] ABC,
  output S0,
  output S1,
  output S2,
  output S3,
  output S4,
  output S5,
  output S6,
  output S7
);

  wire not_1_out, not_2_out, not_3_out, not_4_out, not_5_out, not_6_out, not_7_out, not_8_out, not_9_out,
       not_10_out, not_11_out, not_12_out;

  not not_1 (not_1_out, ABC[2]);
  not not_2 (not_2_out, ABC[1]);
  not not_3 (not_3_out, ABC[0]);
  not not_4 (not_4_out, ABC[2]);
  not not_5 (not_5_out, ABC[1]);
  not not_6 (not_6_out, ABC[2]);
  not not_7 (not_7_out, ABC[0]);
  not not_8 (not_8_out, ABC[2]);
  not not_9 (not_9_out, ABC[1]);
  not not_10 (not_10_out, ABC[0]);
  not not_11 (not_11_out, ABC[1]);
  not not_12 (not_12_out, ABC[0]);
  and and_1 (S7, ABC[2], ABC[1], ABC[0]);
  and and_2 (S0, not_1_out, not_2_out, not_3_out);
  and and_3 (S1, not_4_out, not_5_out, ABC[0]);
  and and_4 (S2, not_6_out, ABC[1], not_7_out);
  and and_5 (S3, not_8_out, ABC[1], ABC[0]);
  and and_6 (S4, ABC[2], not_9_out, not_10_out);
  and and_7 (S5, ABC[2], not_11_out, ABC[0]);
  and and_8 (S6, ABC[2], ABC[1], not_12_out);
endmodule

module Buff (
  input  [3:0] E,
  input  in_2,
  output [3:0] S
);

  assign S[3] = in_2 ? E[3] : 1'bz;  // Controlled_Buffer controlled_buffer_1
  assign S[2] = in_2 ? E[2] : 1'bz;  // Controlled_Buffer controlled_buffer_2
  assign S[0] = in_2 ? E[0] : 1'bz;  // Controlled_Buffer controlled_buffer_3
  assign S[1] = in_2 ? E[1] : 1'bz;  // Controlled_Buffer controlled_buffer_4
endmodule
