// Logisim project somador.circ as structural Verilog: 3 circuits, main circuit main
module main (
);

  aula1 aula1_1 ();  // open: A, B, Cin, S, Vai_1
endmodule

// Add_1
module aula1 (
  input  A,
  input  B,
  input  Cin,
  output S,
  output Vai_1
);

  wire and_1_out, and_2_out, or_1_out, xor_1_out;

  xor xor_1 (xor_1_out, A, B);
  or or_1 (or_1_out, Cin, B);
  xor xor_2 (S, xor_1_out, Cin);
  and and_1 (and_1_out, or_1_out, A);
  and and_2 (and_2_out, B, Cin);
  or or_2 (Vai_1, and_1_out, and_2_out);
endmodule

module somador4bit (
  input  A,
  input  B,
  input  Cin,
  input  in_4,
  input  in_5,
  input  in_6,
  input  in_7,
  input  in_8,
  input  in_9,
  output [3:0] out_10
);

  wire aula1_1_vai_1, aula1_2_vai_1, aula1_3_vai_1;

  aula1 aula1_1 (.A(A), .B(B), .Cin(Cin), .S(out_10[0]), .Vai_1(aula1_1_vai_1));
  aula1 aula1_2 (.A(in_4), .B(in_5), .Cin(aula1_1_vai_1), .S(out_10[1]), .Vai_1(aula1_2_vai_1));
  aula1 aula1_3 (.A(in_7), .B(in_6), .Cin(aula1_2_vai_1), .S(out_10[2]), .Vai_1(aula1_3_vai_1));
  aula1 aula1_4 (.A(in_9), .B(in_8), .Cin(aula1_3_vai_1), .S(out_10[3]));  // open: Vai_1
endmodule
